# Fritzing sketch sispro (saved by Fritzing 0.8.3b)

parts:
  LED1_(Mode) = LED - 3mm [color="Green (570nm)" package="3 mm [THT]"]
  R1 = Resistor [tolerance=±5% resistance=47 package=THT]
  S1_(Shutdown) = Pushbutton [package=THT]
  Raspberry_Pi_rev1 = Raspberry Pi rev2
  S2_(Reset) = Pushbutton [package=THT]
  S3_(Mode) = Pushbutton [package=THT]
  LED2_(Power) = LED - 3mm [color="Red (660nm)" package="3 mm [THT]"]
  R2 = Resistor [tolerance=±5% resistance=68 package=THT]
  GPS_Breakout_Board = IC, SIP package, 9 pins [chip_label=GPS]
  LED3_(GPS) = LED - 3mm [color="Blue (525nm)" package="3 mm [THT]"]
  R3 = Resistor [tolerance=±5% resistance=47 package=THT]

nets:
  N1: LED1_(Mode).cathode, R1.Pin_0
  N2: LED1_(Mode).anode, Raspberry_Pi_rev1.GPIO4
  N3: R1.Pin_1, S1_(Shutdown).leg0, Raspberry_Pi_rev1.GND, S2_(Reset).leg0, S3_(Mode).leg0, R2.Pin_1, GPS_Breakout_Board.pin7, R3.Pin_1
  N4: S1_(Shutdown).leg1, Raspberry_Pi_rev1.GPIO_27
  N5: Raspberry_Pi_rev1.3V3, GPS_Breakout_Board.pin8
  N6: Raspberry_Pi_rev1.GPIO_23, LED2_(Power).anode
  N7: Raspberry_Pi_rev1.GPIO_14, GPS_Breakout_Board.pin6
  N8: Raspberry_Pi_rev1.GPIO_15, GPS_Breakout_Board.pin5
  N9: Raspberry_Pi_rev1.GPIO_17, S3_(Mode).leg1
  N10: Raspberry_Pi_rev1.GPIO_22, S2_(Reset).leg1
  N11: LED2_(Power).cathode, R2.Pin_0
  N12: GPS_Breakout_Board.pin4, LED3_(GPS).anode
  N13: LED3_(GPS).cathode, R3.Pin_0
